# Fritzing sketch vehicle_schematic (saved by Fritzing 1.0.0d)
breadboards: 2

parts:
  Raspberry_Pi_1 = Raspberry Pi 3 [part_number=RPI-3-V1.2]
  M1 = RioRand LM2596
  Part1 = Arduino Mega ADK (Rev3)
  S1 = H-Bridge with L298N
  U2 = LIPO-1000mAh [package=lipo-1000]
  U3 = LIPO-1000mAh [package=lipo-1000]
  U4 = LIPO-1000mAh [package=lipo-1000]
  Left_Sensor = HC-SR04 Ultrasonic Distance Sensor
  Right_sensor = HC-SR04 Ultrasonic Distance Sensor
  Back_sensor = HC-SR04 Ultrasonic Distance Sensor
  Front_sensor = HC-SR04 Ultrasonic Distance Sensor
  M6 = gy9250
  M7 = DC Motor [voltage_(max)=6V voltage_(min)=3V]
  M8 = DC Motor [voltage_(max)=6V voltage_(min)=3V]

nets:
  N1: Raspberry_Pi_1.GND, M1.Pin_4
  N2: Raspberry_Pi_1.5V, M1.Pin_3
  VIN: M1.Pin_1, Part1.VIN, S1.12V, U4.+
  GND: M1.Pin_2, Part1.GND, S1.GND, U2.-, Left_Sensor.GND, Right_sensor.GND, Back_sensor.GND, Front_sensor.GND, M6.pin2
  N3: Part1.D21/SCL, M6.pin3
  N4: Part1.D20/SDA, M6.pin4
  N5: Part1.D13_PWM, Front_sensor.TRIG
  N6: Part1.D12_PWM, Front_sensor.ECHO
  N7: Part1.D11_PWM, Left_Sensor.TRIG
  N8: Part1.D10_PWM, Left_Sensor.ECHO
  N9: Part1.D9_PWM, Right_sensor.TRIG
  N10: Part1.D8_PWM, Right_sensor.ECHO
  VCC: Part1.IOREF, Part1.5V, Left_Sensor.VCC, Right_sensor.VCC, Back_sensor.VCC, Front_sensor.VCC, M6.pin1
  N11: Part1.D2_PWM, S1.IN3
  N12: Part1.D3_PWM, S1.IN2
  N13: Part1.D4_PWM, S1.IN1
  N14: Part1.D5_PWM, S1.ENA
  N15: Part1.D6_PWM, Back_sensor.ECHO
  N16: Part1.D7_PWM, Back_sensor.TRIG
  N17: Part1.D22, S1.IN4
  N18: Part1.D23, S1.ENB
  N19: S1.M1-01, M8.pin_1
  N20: S1.M1-02, M8.pin_2
  N21: S1.M2-01, M7.pin_2
  N22: S1.M2-02, M7.pin_1
  N23: U2.+, U3.-
  N24: U3.+, U4.-

custom parts:
  H-Bridge with L298N: h-bridge
  gy9250: MPU-9250 module (three-axis gyroscope + three-axis acceleration + three-axis magnetic field). The generic model from ebay et. al. rather than the Sparkfun version.

// code stored in the sketch: driver.ino
#include <LiquidCrystal_I2C.h>

////////////////////////////////////////////////////////
//                Ultrasonic Sensors                  //
////////////////////////////////////////////////////////
#define S1_T  6
#define S1_E  7
#define S2_T 13
#define S2_E 12
#define S3_T  8
#define S3_E  9
#define S4_T 10
#define S4_E 11

////////////////////////////////////////////////////////
//                  Motor Driver                      //
////////////////////////////////////////////////////////
#define ENA  4
#define IN1 50
#define IN2 51
#define IN3 48
#define IN4 49
#define ENB  5

#define MIN_DIST_THRESHOLD 20

#define PRINT_DISTANCE(IDENT, TP, EP) \
  Serial.print(#IDENT); \
  Serial.print(": "); \
  Serial.print(read_distance_from_sensor(TP, EP)); \
  Serial.println("cm"); \

#define ENABLE_ULTRASONIC_SENSOR(TP, EP) \
  pinMode(TP, OUTPUT); \
  pinMode(EP, INPUT); \

#define BLOCK_UNTIL_FAR_FROM_OBSTACLE() \
    while (read_distance_from_sensor(S1_T, S1_E) <= MIN_DIST_THRESHOLD \
          && !(read_distance_from_sensor(S4_T, S4_E) <= MIN_DIST_THRESHOLD)) {} \

LiquidCrystal_I2C lcd(0x27, 16, 2);

const float read_distance_from_sensor(int trig_pin, int echo_pin) {
  delay(55);
  // Clear trigger pin if it was high previously
  digitalWrite(trig_pin, LOW);
  
  digitalWrite(trig_pin, HIGH);
  delayMicroseconds(10);
  digitalWrite(trig_pin, LOW);

  const float duration = pulseIn(echo_pin, HIGH);
  const float distance = 0.0344 * duration / 2;
  if (distance > 1000) {
    return 0;
  }
  return distance;
}

void go_forward() {
  digitalWrite(IN1, LOW);
  digitalWrite(IN2, HIGH);
}

void go_backward() {
  digitalWrite(IN1, HIGH);
  digitalWrite(IN2, LOW);
}

void turn_right() {
  digitalWrite(IN3, LOW);
  digitalWrite(IN4, HIGH);
}

void turn_left() {
  digitalWrite(IN3, HIGH);
  digitalWrite(IN4, LOW);
}

void stop_turn() {
  digitalWrite(IN3, LOW);
  digitalWrite(IN4, LOW);
}

void setup() {
  // init the lcd
  lcd.init();
  lcd.clear();
  lcd.backlight();

  lcd.setCursor(0, 0);
  lcd.print("Patrick 0.1");
  
  ENABLE_ULTRASONIC_SENSOR(S1_T, S1_E);
  ENABLE_ULTRASONIC_SENSOR(S2_T, S2_E);
  ENABLE_ULTRASONIC_SENSOR(S3_T, S3_E);
  ENABLE_ULTRASONIC_SENSOR(S4_T, S4_E);

  // Set up the motor driver
  pinMode(ENA, OUTPUT);
  pinMode(IN1, OUTPUT);
  pinMode(IN2, OUTPUT);
  pinMode(IN3, OUTPUT);
  pinMode(IN4, OUTPUT);
  pinMode(ENB, OUTPUT);

  analogWrite(ENA, 255);
  analogWrite(ENB, 255);
  go_forward();

  Serial.begin(9600);
}

void loop() {
  PRINT_DISTANCE(S1, S1_T, S1_E);
  PRINT_DISTANCE(S2, S2_T, S2_E);
  PRINT_DISTANCE(S3, S3_T, S3_E);
  PRINT_DISTANCE(S4, S4_T, S4_E);

  const float s1_d = read_distance_from_sensor(S1_T, S1_E);
  if (s1_d <= MIN_DIST_THRESHOLD * 2) {
    go_backward();
    BLOCK_UNTIL_FAR_FROM_OBSTACLE();

    const float s2_d = read_distance_from_sensor(S2_T, S2_E);
    const float s3_d = read_distance_from_sensor(S3_T, S3_E);
    go_forward();
    if (s2_d > s3_d) {
      lcd.setCursor(0, 1);
      lcd.print("R");
      turn_right();
    } else {
      lcd.setCursor(0, 1);
      lcd.print("L");
      turn_left();
    }

    delay(1500);
    lcd.setCursor(0, 1);
    lcd.print("N");
    stop_turn();
  }
}

// code stored in the sketch: Untitled2.ino
#include <LiquidCrystal_I2C.h>

////////////////////////////////////////////////////////
//                Ultrasonic Sensors                  //
////////////////////////////////////////////////////////
#define S1_T  6
#define S1_E  7
#define S2_T 13
#define S2_E 12
#define S3_T  8
#define S3_E  9
#define S4_T 10
#define S4_E 11

////////////////////////////////////////////////////////
//                  Motor Driver                      //
////////////////////////////////////////////////////////
#define ENA  4
#define IN1 50
#define IN2 51
#define IN3 48
#define IN4 49
#define ENB  5

#define MIN_DIST_THRESHOLD 20

#define PRINT_DISTANCE(IDENT, TP, EP) \
  Serial.print(#IDENT); \
  Serial.print(": "); \
  Serial.print(read_distance_from_sensor(TP, EP)); \
  Serial.println("cm"); \

#define ENABLE_ULTRASONIC_SENSOR(TP, EP) \
  pinMode(TP, OUTPUT); \
  pinMode(EP, INPUT); \

#define BLOCK_UNTIL_FAR_FROM_OBSTACLE() \
    while (read_distance_from_sensor(S1_T, S1_E) <= MIN_DIST_THRESHOLD \
          && !(read_distance_from_sensor(S4_T, S4_E) <= MIN_DIST_THRESHOLD)) {} \

LiquidCrystal_I2C lcd(0x27, 16, 2);

const float read_distance_from_sensor(int trig_pin, int echo_pin) {
  delay(55);
  // Clear trigger pin if it was high previously
  digitalWrite(trig_pin, LOW);
  
  digitalWrite(trig_pin, HIGH);
  delayMicroseconds(10);
  digitalWrite(trig_pin, LOW);

  const float duration = pulseIn(echo_pin, HIGH);
  const float distance = 0.0344 * duration / 2;
  if (distance > 1000) {
    return 0;
  }
  return distance;
}

void go_forward() {
  digitalWrite(IN1, LOW);
  digitalWrite(IN2, HIGH);
}

void go_backward() {
  digitalWrite(IN1, HIGH);
  digitalWrite(IN2, LOW);
}

void turn_right() {
  digitalWrite(IN3, LOW);
  digitalWrite(IN4, HIGH);
}

void turn_left() {
  digitalWrite(IN3, HIGH);
  digitalWrite(IN4, LOW);
}

void stop_turn() {
  digitalWrite(IN3, LOW);
  digitalWrite(IN4, LOW);
}

void setup() {
  // init the lcd
  lcd.init();
  lcd.clear();
  lcd.backlight();

  lcd.setCursor(0, 0);
  lcd.print("Patrick 0.1");
  
  ENABLE_ULTRASONIC_SENSOR(S1_T, S1_E);
  ENABLE_ULTRASONIC_SENSOR(S2_T, S2_E);
  ENABLE_ULTRASONIC_SENSOR(S3_T, S3_E);
  ENABLE_ULTRASONIC_SENSOR(S4_T, S4_E);

  // Set up the motor driver
  pinMode(ENA, OUTPUT);
  pinMode(IN1, OUTPUT);
  pinMode(IN2, OUTPUT);
  pinMode(IN3, OUTPUT);
  pinMode(IN4, OUTPUT);
  pinMode(ENB, OUTPUT);

  analogWrite(ENA, 255);
  analogWrite(ENB, 255);
  go_forward();

  Serial.begin(9600);
}

void loop() {
  PRINT_DISTANCE(S1, S1_T, S1_E);
  PRINT_DISTANCE(S2, S2_T, S2_E);
  PRINT_DISTANCE(S3, S3_T, S3_E);
  PRINT_DISTANCE(S4, S4_T, S4_E);

  const float s1_d = read_distance_from_sensor(S1_T, S1_E);
  if (s1_d <= MIN_DIST_THRESHOLD * 2) {
    go_backward();
    BLOCK_UNTIL_FAR_FROM_OBSTACLE();

    const float s2_d = read_distance_from_sensor(S2_T, S2_E);
    const float s3_d = read_distance_from_sensor(S3_T, S3_E);
    go_forward();
    if (s2_d > s3_d) {
      lcd.setCursor(0, 1);
      lcd.print("R");
      turn_right();
    } else {
      lcd.setCursor(0, 1);
      lcd.print("L");
      turn_left();
    }

    delay(1500);
    lcd.setCursor(0, 1);
    lcd.print("N");
    stop_turn();
  }
}
